# Fritzing sketch UFO-LAMP (saved by Fritzing 0.9.4)
circuit board: 10.0207cm x 6.66753cm
breadboards: 1

parts:
  Q2 = npn-Powertransistor [package="TO220 [THT]"]
  NodeMCU = Gizwits WiFi Witty ESP-12F
  Q3 = npn-Powertransistor [package="TO220 [THT]"]
  Q4 = npn-Powertransistor [package="TO220 [THT]"]
  Q5 = npn-Powertransistor [package="TO220 [THT]"]
  Q6 = npn-Powertransistor [package="TO220 [THT]"]
  R1 = Resistor [tolerance=±5% resistance=1 package=THT]
  R2 = Resistor [tolerance=±5% resistance=1 package=THT]
  R3 = Resistor [tolerance=±5% resistance=1 package=THT]
  R4 = Resistor [tolerance=±5% resistance=1 package=THT]
  R5 = Resistor [tolerance=±5% resistance=1 package=THT]
  R30 = Resistor [tolerance=±5% resistance=68 package=THT]
  R31 = Resistor [tolerance=±5% resistance=68 package=THT]
  R32 = Resistor [tolerance=±5% resistance=68 package=THT]
  R33 = Resistor [tolerance=±5% resistance=68 package=THT]
  R34 = Resistor [tolerance=±5% resistance=68 package=THT]
  R35 = Resistor [tolerance=±5% resistance=68 package=THT]
  R36 = Resistor [tolerance=±5% resistance=68 package=THT]
  R37 = Resistor [tolerance=±5% resistance=68 package=THT]
  R38 = Resistor [tolerance=±5% resistance=68 package=THT]
  R39 = Resistor [tolerance=±5% resistance=68 package=THT]
  R40 = Resistor [tolerance=±5% resistance=68 package=THT]
  R41 = Resistor [tolerance=±5% resistance=68 package=THT]
  R18 = Resistor [tolerance=±5% resistance=68 package=THT]
  R19 = Resistor [tolerance=±5% resistance=68 package=THT]
  R20 = Resistor [tolerance=±5% resistance=68 package=THT]
  R21 = Resistor [tolerance=±5% resistance=68 package=THT]
  R22 = Resistor [tolerance=±5% resistance=68 package=THT]
  R23 = Resistor [tolerance=±5% resistance=68 package=THT]
  R24 = Resistor [tolerance=±5% resistance=68 package=THT]
  R25 = Resistor [tolerance=±5% resistance=68 package=THT]
  R26 = Resistor [tolerance=±5% resistance=68 package=THT]
  R27 = Resistor [tolerance=±5% resistance=68 package=THT]
  R28 = Resistor [tolerance=±5% resistance=68 package=THT]
  R29 = Resistor [tolerance=±5% resistance=68 package=THT]
  R42 = Resistor [tolerance=±5% resistance=68 package=THT]
  R43 = Resistor [tolerance=±5% resistance=68 package=THT]
  R44 = Resistor [tolerance=±5% resistance=68 package=THT]
  R45 = Resistor [tolerance=±5% resistance=68 package=THT]
  R46 = Resistor [tolerance=±5% resistance=68 package=THT]
  R47 = Resistor [tolerance=±5% resistance=68 package=THT]
  Power_plug = Power plug
  LED1 = LEDs [package=led10mm]
  LED2 = LEDs [package=led10mm]
  LED3 = LEDs [package=led10mm]
  LED4 = LEDs [package=led10mm]
  LED5 = LEDs [package=led10mm]
  LED6 = LEDs [package=led10mm]
  LED7 = LEDs [package=led10mm]
  LED8 = LEDs [package=led10mm]
  LED9 = LEDs [package=led10mm]
  LED10 = LEDs [package=led10mm]
  LED11 = LEDs [package=led10mm]
  LED12 = LEDs [package=led10mm]
  LED13 = LEDs [package=led10mm]
  LED14 = LEDs [package=led10mm]
  LED15 = LEDs [package=led10mm]
  LED16 = LEDs [package=led10mm]
  LED17 = LEDs [package=led10mm]
  LED18 = LEDs [package=led10mm]
  LED19 = LEDs [package=led10mm]
  LED20 = LEDs [package=led10mm]
  LED21 = LEDs [package=led10mm]
  LED22 = LEDs [package=led10mm]
  LED23 = LEDs [package=led10mm]
  LED24 = LEDs [package=led10mm]
  LED25 = LEDs [package=led10mm]
  LED26 = LEDs [package=led10mm]
  LED27 = LEDs [package=led10mm]
  LED28 = LEDs [package=led10mm]
  LED29 = LEDs [package=led10mm]
  LED30 = LEDs [package=led10mm]

nets:
  N1: Q2.base, R2.Pin_1
  N2: Q2.collector, R36.Pin_0, R37.Pin_0, R38.Pin_0, R39.Pin_0, R40.Pin_0, R41.Pin_0
  GND: Q2.emitter, NodeMCU.GND, Q3.emitter, Q4.emitter, Q5.emitter, Q6.emitter, Power_plug.GND
  N3: NodeMCU.GPIO14, R4.Pin_1
  N4: NodeMCU.GPIO13, R2.Pin_0
  VCC: NodeMCU.VCC, Power_plug.VCC, LED1.A, LED2.A, LED3.A, LED4.A, LED5.A, LED6.A, LED7.A, LED8.A, LED9.A, LED10.A, LED11.A, LED12.A, LED13.A, LED14.A, LED15.A, LED16.A, LED17.A, LED18.A, LED19.A, LED20.A, LED21.A, LED22.A, LED23.A, LED24.A, LED25.A, LED26.A, LED27.A, LED28.A, LED29.A, LED30.A
  N5: NodeMCU.GPIO15, R5.Pin_1
  N6: NodeMCU.GPIO0, R3.Pin_0
  N7: NodeMCU.GPIO5, R1.Pin_0
  N8: Q3.base, R1.Pin_1
  N9: Q3.collector, R30.Pin_0, R31.Pin_0, R32.Pin_0, R33.Pin_0, R34.Pin_0, R35.Pin_0
  N10: Q4.base, R3.Pin_1
  N11: Q4.collector, R42.Pin_1, R43.Pin_1, R44.Pin_1, R45.Pin_1, R46.Pin_1, R47.Pin_1
  N12: Q5.base, R4.Pin_0
  N13: Q5.collector, R18.Pin_1, R19.Pin_1, R20.Pin_1, R21.Pin_1, R22.Pin_1, R23.Pin_1
  N14: Q6.base, R5.Pin_0
  N15: Q6.collector, R24.Pin_1, R25.Pin_1, R26.Pin_1, R27.Pin_1, R28.Pin_1, R29.Pin_1
  N16: R30.Pin_1, LED23.C
  N17: R31.Pin_1, LED19.C
  N18: R32.Pin_1, LED21.C
  N19: R33.Pin_1, LED20.C
  N20: R34.Pin_1, LED24.C
  N21: R35.Pin_1, LED22.C
  N22: R36.Pin_1, LED3.C
  N23: R37.Pin_1, LED6.C
  N24: R38.Pin_1, LED2.C
  N25: R39.Pin_1, LED4.C
  N26: R40.Pin_1, LED1.C
  N27: R41.Pin_1, LED5.C
  N28: R18.Pin_0, LED10.C
  N29: R19.Pin_0, LED12.C
  N30: R20.Pin_0, LED7.C
  N31: R21.Pin_0, LED11.C
  N32: R22.Pin_0, LED9.C
  N33: R23.Pin_0, LED8.C
  N34: R24.Pin_0, LED25.C
  N35: R25.Pin_0, LED26.C
  N36: R26.Pin_0, LED29.C
  N37: R27.Pin_0, LED30.C
  N38: R28.Pin_0, LED27.C
  N39: R29.Pin_0, LED28.C
  N40: R42.Pin_0, LED18.C
  N41: R43.Pin_0, LED17.C
  N42: R44.Pin_0, LED14.C
  N43: R45.Pin_0, LED13.C
  N44: R46.Pin_0, LED16.C
  N45: R47.Pin_0, LED15.C
